# Fritzing sketch Arduino Wiring Diragram (saved by Fritzing 0.9.9b)
breadboards: 1

parts:
  Part1 = Arduino Uno (Rev3) - ICSP
  HC-SR04_Sensor_1 = HC-SR04 Ultrasonic Distance Sensor
  R1 = Resistor [tolerance=±5% power=0.25 resistance=220 package=THT]
  P2 = Multimeter straight red probe
  Part2 = Current Sensor 5A
  P3 = Multimeter straight black probe
  VM2 = Multimeter (DC Voltage)
  R2 = Resistor [tolerance=±5% power=0.25 resistance=220 package=THT]
  AM1 = Multimeter (AC Current)  # not connected

nets:
  N1: Part1.A0, R1.Pin_0, VM2.V_Probe, R2.Pin_0
  N2: Part1.A1, Part2.2, Part2.OUT
  N3: Part1.D9_PWM, HC-SR04_Sensor_1.ECHO
  N4: Part1.D10_PWM/SS, HC-SR04_Sensor_1.TRIG
  GND: Part1.GND, HC-SR04_Sensor_1.GND, Part2.GND, P3.Probe_tip, P3.Probe_meter_end, VM2.COM_Probe, R2.Pin_1
  VCC: Part1.5V, HC-SR04_Sensor_1.VCC, Part2.VCC
  N5: R1.Pin_1, P2.Probe_tip, P2.Probe_meter_end
